# Fritzing sketch aProjector (saved by Fritzing 0.9.3b)
breadboards: 1

parts:
  hc-sr1 = hc-sr04
  R1 = Resistor [tolerance=±5% resistance=2.2k package="0603 [SMD]"]
  R2 = Resistor [tolerance=±5% resistance=3.3k package="0603 [SMD]"]
  Pololu_A1 = Pololu A4988 [package=SO16]
  SW1 = DIP SWITCH [package=dipswitch-02]
  M1 = Stepper Motor - Bipolar
  VCC1 = Battery block 9V
  C1 = Electrolytic Capacitor [capacitance=10µF package="100 mil [THT, electrolytic]"]
  R3 = Resistor [tolerance=±5% resistance=220 package="0603 [SMD]"]

nets:
  N1: hc-sr1.Echo, R1.Pin_0
  N2: hc-sr1.GND, R2.Pin_1, Pololu_A1.GND#8, R3.Pin_1
  N3: R1.Pin_1, R2.Pin_0
  N4: Pololu_A1.RESET, Pololu_A1.SLEEP
  N5: Pololu_A1.VDD, SW1.4
  N6: Pololu_A1.1B, M1.D
  N7: Pololu_A1.1A, M1.B
  N8: Pololu_A1.2A, M1.C
  N9: Pololu_A1.2B, M1.A
  N10: Pololu_A1.GND#14, VCC1.-, C1.-
  N11: Pololu_A1.VMOT, VCC1.+, C1.+
  N12: SW1.1, R3.Pin_0
